# Fritzing sketch SmartDesk (saved by Fritzing 0.9.4)
breadboards: 1

parts:
  Argon1 = Particle Argon
  WS2812B1 = WS2812B [package="DIP (Dual Inline) [THT]"]
  Load_Cell1 = Load Cell - Red/white/black/green
  Part1 = HX711 Weighing Sensor Module
  Part2 = Ambient Light Sensor (TEMT6000 Breakout Board)
  Finger_Print_Sensor = Camdenboss CTB0158-4 [part_number=CTB0158-4 package=THT]
  Touch_Screen = OLED 128x64 I2C Monochrome Display
  microSD1 = MicroSD Card Module

nets:
  VCC: Argon1.3.3V, Part1.VCC, Part2.VCC, Finger_Print_Sensor.VCC, Touch_Screen.VDD, microSD1.VCC
  GND: Argon1.GND, WS2812B1.GND, Part1.GND, Part2.GND, Finger_Print_Sensor.Ground, Touch_Screen.GND, microSD1.GND
  N1: Argon1.A0, Part2.S
  N2: Argon1.A5, microSD1.CS
  N3: Argon1.SCK, microSD1.SCK
  N4: Argon1.MO, microSD1.MOSI
  N5: Argon1.MI, microSD1.MISO
  N6: Argon1.RX, Finger_Print_Sensor.Serial_RX
  N7: Argon1.TX, Finger_Print_Sensor.Serial_TX
  N8: Argon1.SDA, Touch_Screen.SDA
  N9: Argon1.SCL, Touch_Screen.SCK
  N10: Argon1.D6, Part1.DO/RX
  N11: Argon1.D7, Part1.CK/TX
  N12: Argon1.D8, WS2812B1.DI
  N13: Argon1.VUSB, WS2812B1.5V
  N14: Load_Cell1.wire1, Part1.E+
  N15: Load_Cell1.wire2, Part1.A+
  N16: Load_Cell1.wire3, Part1.E-
  N17: Load_Cell1.wire4, Part1.A-

custom parts:
  Particle Argon: The Argon is a powerful Wi-Fi enabled development board that can act as either a standalone Wi-Fi endpoint or Wi-Fi enabled gateway for Particle Mesh networks. It is based on the Nordic nRF52840 and has built-in battery charging circuitry so it’s easy to connect a Li-Po and deploy your local network in minutes. The Argon is great for connecting existing projects to the Particle Device Cloud or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
  WS2812B: Adafruit NeoPixel Breakout
  Load Cell - Red/white/black/green: A rectangle load cell/weighting pressure Sensor with four wires - Red, white, black, green. Normally corresponding with E+, E-, A+, A- respectively.
  Camdenboss CTB0158-4: Camdenboss CTB0158-4 5.08mm (0.2") Pitch Standard Profile 90 ̊ Rising Clamp Terminal, 4 pole The real-life connectors are modular, made up of two or three connector blocks slotted together. These can be further slotted together to make larger connectors. Fritzing part is derived from Screw terminals by Lionel Michel. Because of the offset between connection pins and screw terminals, these are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
